// Logisim project EX1.circ as structural Verilog: 2 circuits, main circuit main
module main (
  input  in_1
);
endmodule

module EX_1 (
  input  C,
  input  H,
  input  M,
  output D
);

  wire and_1_out, and_2_out;

  and and_1 (and_1_out, C, M);
  and and_2 (and_2_out, C, H);
  or or_1 (D, and_1_out, and_2_out);
endmodule
