// Logisim project EX10.circ as structural Verilog
module EX10 (
  input  S,
  input  K,
  input  A,
  input  P,
  output D
);

  wire and_1_out;

  and and_1 (and_1_out, S, K);
  or or_1 (D, P, A, and_1_out);
endmodule
