// Logisim project EX2.circ as structural Verilog
module EX2 (
  input  V,
  input  P,
  input  H,
  output R
);

  wire and_1_out, not_1_out;

  not not_1 (not_1_out, H);
  and and_1 (and_1_out, V, not_1_out);
  or or_1 (R, P, and_1_out);
endmodule
