// Logisim project EX3.circ as structural Verilog
module EX3 (
  input  T,
  input  P,
  input  J,
  input  H,
  output V
);

  wire and_1_out, and_2_out, not_1_out;

  not not_1 (not_1_out, J);
  and and_1 (and_1_out, not_1_out, H);
  and and_2 (and_2_out, T, P);
  or or_1 (V, and_1_out, and_2_out);
endmodule
