// Logisim project EX4.circ as structural Verilog
module EX4 (
  input  P,
  input  M,
  input  H,
  input  A,
  output D
);

  wire and_1_out, and_2_out, not_1_out, not_2_out;

  and and_1 (and_1_out, M, not_1_out);
  not not_1 (not_1_out, H);
  and and_2 (and_2_out, P, not_2_out);
  not not_2 (not_2_out, H);
  or or_1 (D, A, and_1_out, and_2_out);
endmodule
