// Logisim project EX5.circ as structural Verilog
module EX5 (
  input  U,
  input  C,
  input  H,
  output I
);

  wire and_1_out, not_1_out;

  not not_1 (not_1_out, C);
  and and_1 (and_1_out, U, not_1_out);
  or or_1 (I, H, and_1_out);
endmodule
