// Logisim project EX6.circ as structural Verilog
module EX6 (
  input  T,
  input  P,
  input  J,
  input  H,
  output A
);

  wire and_1_out, and_2_out;

  and and_1 (and_1_out, J, H);
  and and_2 (and_2_out, T, P);
  or or_1 (A, and_1_out, and_2_out);
endmodule
