// Logisim project EX7.circ as structural Verilog
module EX7 (
  input  C,
  input  V,
  input  S,
  input  A,
  input  P,
  output E
);

  wire and_1_out, and_2_out;

  and and_1 (and_1_out, S, P);
  and and_2 (and_2_out, C, V);
  or or_1 (E, and_1_out, and_2_out);
endmodule
