// Logisim project EX8.circ as structural Verilog
module EX8 (
  input  E,
  input  P,
  input  D,
  input  R,
  output A
);

  wire and_1_out, and_2_out;

  and and_1 (and_1_out, D, R);
  and and_2 (and_2_out, E, P);
  or or_1 (A, and_1_out, and_2_out);
endmodule
