// Logisim project EX9.circ as structural Verilog
module EX9 (
  input  P,
  input  L,
  input  H,
  input  I,
  output A
);

  wire and_1_out, and_2_out, not_1_out;

  and and_1 (and_1_out, L, H);
  and and_2 (and_2_out, P, not_1_out);
  not not_1 (not_1_out, L);
  or or_1 (A, I, and_1_out, and_2_out);
endmodule
